// Logisim project 332_pipelined.circ as structural Verilog: 4 circuits, main circuit main
module main (
  input  [7:0] in_1,
  output [3:0] oppcode,
  output [1:0] rs,
  output [1:0] rt,
  output [1:0] rd,
  output I_f_flag,
  output R_f_flag,
  output [9:0] RS_Data,
  output [9:0] RT_Data,
  output [9:0] RD_Data
);

  wire Clk, L_S_flag;
  wire [1:0] R_opp;
  wire [7:0] adder_1_out, PC_q;
  wire [9:0] IM, mem_data, RDd;

  Clock Clock (.out(Clk));
  Register PC (.D(adder_1_out), .Q(PC_q), .clk(Clk));  // open: en, clr
  Adder adder_1 (.a(PC_q), .b(in_1), .out(adder_1_out));  // open: cin, cout
  ROM #(.dataWidth(10)) rom_1 (.addr(PC_q), .data({oppcode, rs, rt, rd}));  // open: sel
  RAM #(.addrWidth(10), .dataWidth(10)) ram_1 (.addr(RD_Data), .data(mem_data), .ld(L_S_flag));  // open: sel, clk, clr
  Multiplexer #(.width(10), .enable("false")) multiplexer_1 (.in0(RD_Data), .in1(mem_data), .out(RDd), .sel(L_S_flag));
  Control control_1 (.oppcode(oppcode), .Format_F(I_f_flag), .R_format(R_opp), .L_S_flag(L_S_flag));
  assign IM = {{8{1'b0}}, rd};  // Bit_Extender bit_extender_1
  Register_FIle register_file_1 (
    .Write_Reg(rd), .Write_Data(RDd), .Ven_EN(I_f_flag), .Clock(Clk), .Read_Data1(RS_Data), .Read_Reg1(rs),
    .Read_Data_2(RT_Data), .Read_Reg2(rt));
  ALU alu_1 (.RS(RS_Data), .RT(RT_Data), .Select_Opperation(R_opp), .OUTPUT(RD_Data));  // open: Cin, Cout
  not not_1 (R_f_flag, I_f_flag);

  // Other names for the same wires on the sheet: opp_C[3:0] = oppcode; ALU_out[9:0] = RD_Data; Fflg = I_f_flag;
  //   RSd[9:0] = RS_Data; RTd[9:0] = RT_Data

  // Notes on the sheet:
  //   instruction mem
  //   1.oppcode, 2. rs, 3.rt, 4.rd
  //   Data mem
  //   contents of rom_1 (hex, n*v repeats v):
  //   111 100 0 0 111 5*0 111 21*0 111
endmodule

// REG FILE
module Register_FIle (
  input  [9:0] Write_Data,
  input  [1:0] Write_Reg,
  input  Ven_EN,
  input  Clock,
  input  [1:0] Read_Reg1,
  input  [1:0] Read_Reg2,
  output [9:0] Read_Data1,
  output [9:0] Read_Data_2
);

  wire R1, R2, R3, R4;
  wire [9:0] Dout1, Dout2, Dout3, Dout4;

  Decoder #(.select(2)) decoder_1 (.out0(R1), .out1(R2), .out2(R4), .out3(R3), .sel(Write_Reg), .en(Ven_EN));
  Register #(.width(10)) u_R1 (.D(Write_Data), .en(R1), .Q(Dout1), .clk(Clock));  // open: clr
  Register #(.width(10)) u_R3 (.D(Write_Data), .en(R3), .Q(Dout3), .clk(Clock));  // open: clr
  Register #(.width(10)) u_R2 (.D(Write_Data), .en(R2), .Q(Dout2), .clk(Clock));  // open: clr
  Register #(.width(10)) u_R4 (.D(Write_Data), .en(R4), .Q(Dout4), .clk(Clock));  // open: clr
  Multiplexer #(.select(2), .width(10), .enable("false")) multiplexer_1 (
    .in0(Dout1), .in1(Dout2), .in2(Dout4), .in3(Dout3), .out(Read_Data1), .sel(Read_Reg1));
  Multiplexer #(.select(2), .width(10), .enable("false")) multiplexer_2 (
    .in0(Dout1), .in1(Dout2), .in2(Dout4), .in3(Dout3), .out(Read_Data_2), .sel(Read_Reg2));

  // Other names for the same wires on the sheet: clk = Clock; Din[9:0] = Write_Data; do1[9:0] = Read_Data1;
  //   do2[9:0] = Read_Data_2; en = Ven_EN; RD1[1:0] = Read_Reg1; RD2[1:0] = Read_Reg2; writeReg[1:0] = Write_Reg
endmodule

module ALU (
  input  [1:0] Select_Opperation,
  input  Cin,
  input  [9:0] RS,
  input  [9:0] RT,
  output Cout,
  output [9:0] OUTPUT
);

  wire [9:0] Add, And, Or, Sub;

  assign And = RS & RT;  // AND_Gate and_1, 10 bits wide
  assign Or = RS | RT;  // OR_Gate or_1, 10 bits wide
  Adder #(.width(10)) adder_1 (.a(RS), .b(RT), .out(Add), .cin(Cin), .cout(Cout));
  Subtractor #(.width(10)) subtractor_1 (.a(RS), .b(RT), .out(Sub), .bin(Cin), .bout(Cout));
  Multiplexer #(.select(2), .width(10), .enable("false")) multiplexer_1 (
    .in0(And), .in1(Or), .in2(Add), .in3(Sub), .out(OUTPUT), .sel(Select_Opperation));

  // Other names for the same wires on the sheet: mIn[1:0] = Select_Opperation; Result[9:0] = OUTPUT; RSin[9:0] = RS;
  //   RTin[9:0] = RT
endmodule

// Format Detector
module Control (
  input  [3:0] oppcode,
  output [1:0] R_format,
  output Format_F,
  output L_S_flag
);

  wire R, undriven;

  Multiplexer multiplexer_1 (.in0(1'b0), .in1(1'b1), .out(Format_F), .sel(oppcode[3]));  // open: en
  not not_1 (R, Format_F);
  Multiplexer #(.select(2), .width(2)) multiplexer_2 (
    .in0(2'b00), .in1(2'b01), .in2(2'b10), .in3(2'b11), .out(R_format), .sel(oppcode[1:0]), .en(R));
  Multiplexer #(.select(2)) multiplexer_3 (
    .in0(1'b1), .in1(1'b0), .in2(1'b1), .in3(undriven), .out(L_S_flag), .sel(oppcode[1:0]), .en(Format_F));

  // Other names for the same wires on the sheet: I = Format_F; opp[1:0] = oppcode[1:0]; format = oppcode[3]

  // Notes on the sheet:
  //   it will check for type and will give  0 for r format, 1 for I format
endmodule
